# Fritzing sketch Fritzing QRcode Diagram (saved by Fritzing 0.9.3b)
breadboards: 1

parts:
  Raspberry_Pi_3 = Raspberry Pi 3 [part_number=RPI-3-V1.2]
  Part3 = RFID USB Reader
  U3 = TRANSCHIPTC5747 [package=camera_sfv24r-2st_2]  # not connected

nets:
  3V3: Raspberry_Pi_3.3v3, Part3.VCC
  N1: Raspberry_Pi_3.GPIO10, Part3.ANT1
  N2: Raspberry_Pi_3.GPIO9, Part3.ANT2
  N3: Raspberry_Pi_3.GPIO11, Part3.CP
  N4: Raspberry_Pi_3.GPIO8, Part3.GNDT
  N5: Raspberry_Pi_3.GPIO25, Part3.GND
  N6: Raspberry_Pi_3.GND, Part3.TX-O

notes:
  Pi camera Ribbon Cable
  Camera
  Raspberry pi 4
  Card Reader RFID
